// Logisim project half adder circuit using NOR gates.circ as structural Verilog: 1 circuit, main circuit main
module main (
  input  A,
  input  B,
  output out_3,
  output out_4
);

  wire nor_1_out, nor_2_out, nor_4_out;

  nor nor_1 (nor_1_out, A, B);
  nor nor_2 (nor_2_out, A, A);
  nor nor_3 (out_3, nor_2_out, nor_4_out);
  nor nor_4 (nor_4_out, B, B);
  nor nor_5 (out_4, out_3, nor_1_out);
endmodule
